# Fritzing sketch Untitled Sketch 2 (saved by Fritzing 0.9.3b)
breadboards: 1

parts:
  Part1 = Breakout Board for Electret Microphone
  Part2 = Arduino Leonardo (Rev3b)
  U1 = BUTTON-CONDUCTIVE [package=button-conductive]
  U2 = ESP8266 WiFi Module [part_number=ESP8266]
  R1 = Resistor [tolerance=±5% resistance=2k package="0402 [SMD]"]
  R2 = Resistor [tolerance=±5% resistance=1k package="0402 [SMD]"]

nets:
  VCC: Part1.VCC, Part2.3V3, U1.1, U2.VCC, U2.CH_PD
  GND: Part1.GND, Part2.GND, U2.GND, R1.Pin_0
  N1: Part1.AUD, Part2.A4
  N2: Part2.D5_PWM, U2.TXD
  N3: Part2.D6_PWM/A7, R2.Pin_1
  N4: Part2.D7, U1.2
  N5: U2.RXD, R1.Pin_1, R2.Pin_0

custom parts:
  ESP8266 WiFi Module: Generic WiFi Module based on the ESP8266 with onboard PCB antenna and UART communications
